// Logisim project Lab02_Bool.circ as structural Verilog: 3 circuits, main circuit main
module main (
  input  A1,
  input  B1,
  input  C1,
  input  A2,
  input  B2,
  input  C2,
  input  D2,
  output Out1,
  output True2
);

  Equation_1 equation_1_1 (.ln1A(A1), .ln1B(B1), .ln1C(C1), .out_4(Out1));
  Equation_2 equation_2_1 (.In2A(A2), .In2B(B2), .In2C(C2), .In2D(D2), .out_5(True2));

  // Notes on the sheet:
  //   Askar Aibar, Lab 2, 20.08.2024
  //   In1A
  //   In1B
  //   In1C
  //   True1
endmodule

module Equation_2 (
  input  In2A,
  input  In2B,
  input  In2C,
  input  In2D,
  output out_5
);

  wire and_1_out, and_2_out, and_3_out, and_4_out;

  and and_1 (and_1_out, ~In2A, ~In2B, In2C, ~In2D);  // AND_Gate
  and and_2 (and_2_out, ~In2A, In2B, In2C, In2D);  // AND_Gate
  and and_3 (and_3_out, In2A, ~In2B, In2C, ~In2D);  // AND_Gate
  and and_4 (and_4_out, In2A, In2B, In2C, ~In2D);  // AND_Gate
  or or_1 (out_5, and_1_out, and_2_out, and_3_out, and_4_out);
endmodule

module Equation_1 (
  input  ln1A,
  input  ln1B,
  input  ln1C,
  output out_4
);

  wire and_1_out, and_2_out, and_3_out;

  and and_1 (and_1_out, ~ln1A, ln1B, ~ln1C);  // AND_Gate
  and and_2 (and_2_out, ln1A, ~ln1B, ~ln1C);  // AND_Gate
  and and_3 (and_3_out, ln1A, ln1B, ln1C);
  or or_1 (out_4, and_1_out, and_2_out, and_3_out);
endmodule
