// Logisim project lab05.circ as structural Verilog: 6 circuits, main circuit main
module main (
  input  reset,
  input  [2:0] Sel,
  output [3:0] out_3,
  output [3:0] out_4,
  output [3:0] out_5,
  output [3:0] out_6,
  output [3:0] out_7,
  output [3:0] out_8
);

  wire clk_out, clock_1_out, clock_2_out, clock_3_out, clock_4_out;

  Clock sysclk ();  // open: out
  Clock clock_1 (.out(clock_1_out));
  Clock clock_2 (.out(clock_2_out));
  Clock clock_3 (.out(clock_3_out));
  Clock clock_4 (.out(clock_4_out));
  Clock clk (.out(clk_out));
  Up up_1 (.clk(clk_out), .rst(reset), .out_3(out_3));
  Down down_1 (.in_1(clock_1_out), .in_2(reset), .out_3(out_4));
  Asynch asynch_1 (.in_1(clock_2_out), .in_2(reset), .out_3(out_5));
  Synch synch_1 (.in_1(clock_3_out), .in_2(reset), .out_3(out_7));
  Johnson johnson_1 (.in_1(clock_4_out), .in_2(reset), .Johnson(out_8));
  Multiplexer #(.select(3), .width(4)) multiplexer_1 (
    .in0(out_3), .in1(out_4), .in2(out_5), .in3(out_7), .in4(out_8), .out(out_6), .sel(Sel));  // open: in5, in6, in7
  Hex_Digit_Display hex_digit_display_1 (.value(out_6));  // open: dp
endmodule

module Up (
  input  clk,
  input  rst,
  output [3:0] out_3
);

  wire d_ff_1_qn, d_ff_2_qn, d_ff_3_qn, d_ff_4_qn;

  D_Flip_Flop d_ff_1 (.D(d_ff_1_qn), .clk(clk), .Q(out_3[0]), .Qn(d_ff_1_qn), .reset(rst));  // open: preset
  D_Flip_Flop d_ff_2 (.D(d_ff_2_qn), .clk(d_ff_1_qn), .Q(out_3[1]), .Qn(d_ff_2_qn), .reset(rst));  // open: preset
  D_Flip_Flop d_ff_3 (.D(d_ff_3_qn), .clk(d_ff_2_qn), .Q(out_3[2]), .Qn(d_ff_3_qn), .reset(rst));  // open: preset
  D_Flip_Flop d_ff_4 (.D(d_ff_4_qn), .clk(d_ff_3_qn), .Q(out_3[3]), .Qn(d_ff_4_qn), .reset(rst));  // open: preset
endmodule

module Down (
  input  in_1,
  input  in_2,
  output [3:0] out_3
);

  wire d_ff_1_qn, d_ff_2_qn, d_ff_3_qn, d_ff_4_qn;

  D_Flip_Flop d_ff_1 (.D(d_ff_1_qn), .clk(in_1), .Q(out_3[0]), .Qn(d_ff_1_qn), .preset(in_2));  // open: reset
  D_Flip_Flop d_ff_2 (.D(d_ff_2_qn), .clk(out_3[0]), .Q(out_3[1]), .Qn(d_ff_2_qn), .preset(in_2));  // open: reset
  D_Flip_Flop d_ff_3 (.D(d_ff_3_qn), .clk(out_3[1]), .Q(out_3[2]), .Qn(d_ff_3_qn), .preset(in_2));  // open: reset
  D_Flip_Flop d_ff_4 (.D(d_ff_4_qn), .clk(out_3[2]), .Q(out_3[3]), .Qn(d_ff_4_qn), .preset(in_2));  // open: reset
endmodule

module Asynch (
  input  in_1,
  input  in_2,
  output [3:0] out_3
);

  wire and_1_out, d_ff_1_qn, d_ff_2_qn, d_ff_3_qn, d_ff_4_qn, or_1_out;

  D_Flip_Flop d_ff_1 (.D(d_ff_1_qn), .clk(in_1), .Q(out_3[0]), .Qn(d_ff_1_qn), .reset(or_1_out));  // open: preset
  or or_1 (or_1_out, in_2, and_1_out);
  D_Flip_Flop d_ff_2 (.D(d_ff_2_qn), .clk(d_ff_1_qn), .Q(out_3[1]), .Qn(d_ff_2_qn), .reset(or_1_out));  // open: preset
  D_Flip_Flop d_ff_3 (.D(d_ff_3_qn), .clk(d_ff_2_qn), .Q(out_3[2]), .Qn(d_ff_3_qn), .reset(or_1_out));  // open: preset
  D_Flip_Flop d_ff_4 (.D(d_ff_4_qn), .clk(d_ff_3_qn), .Q(out_3[3]), .Qn(d_ff_4_qn), .reset(or_1_out));  // open: preset
  and and_1 (and_1_out, out_3[3], out_3[1]);
endmodule

module Synch (
  input  in_1,
  input  in_2,
  output [3:0] out_3
);

  D_Flip_Flop d_ff_1 (.D(out_3[3]), .clk(in_1), .Q(out_3[0]), .preset(in_2));  // open: Qn, reset
  D_Flip_Flop d_ff_2 (.D(out_3[0]), .clk(in_1), .Q(out_3[1]), .reset(in_2));  // open: Qn, preset
  D_Flip_Flop d_ff_3 (.D(out_3[1]), .clk(in_1), .Q(out_3[2]), .reset(in_2));  // open: Qn, preset
  D_Flip_Flop d_ff_4 (.D(out_3[2]), .clk(in_1), .Q(out_3[3]), .reset(in_2));  // open: Qn, preset
endmodule

module Johnson (
  input  in_1,
  input  in_2,
  output [3:0] Johnson
);

  wire d_ff_4_qn;

  D_Flip_Flop d_ff_1 (.D(d_ff_4_qn), .clk(in_1), .Q(Johnson[0]), .preset(in_2));  // open: Qn, reset
  D_Flip_Flop d_ff_2 (.D(Johnson[0]), .clk(in_1), .Q(Johnson[1]), .reset(in_2));  // open: Qn, preset
  D_Flip_Flop d_ff_3 (.D(Johnson[1]), .clk(in_1), .Q(Johnson[2]), .reset(in_2));  // open: Qn, preset
  D_Flip_Flop d_ff_4 (.D(Johnson[2]), .clk(in_1), .Q(Johnson[3]), .Qn(d_ff_4_qn), .reset(in_2));  // open: preset
endmodule
